# Fritzing sketch CircuitPlaygroundHookup (saved by Fritzing 0.9.3b)

parts:
  Part1 = Adafruit Circuit Playground Express [part_number="Adafruit #3333"]
  NEOPIXEL2 = Neopixel Strip -- White (60/m) [part_number=1138]
  NEOPIXEL1 = Neopixel Strip -- White (60/m) [part_number=1138]

nets:
  +5V: Part1.3.3V, NEOPIXEL2.+5V, NEOPIXEL1.+5V
  GND: Part1.GND, NEOPIXEL2.GND, NEOPIXEL1.GND
  N1: Part1.D3_A4_SCL, NEOPIXEL1.DI
  N2: Part1.D2_A5_SDA, NEOPIXEL2.DI

custom parts:
  Adafruit Circuit Playground Express: Circuit Playground Express is the next step towards a perfect introduction to electronics and programming. We've taken the original Circuit Playground Classic and made it even better! Not only did we pack even more sensors in, we also made it even easier to program. You can now start your journey with Microsoft MakeCode block-based or Javascript programming. Then, you can use the same board to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
  Neopixel Strip -- White (60/m): Neopixel Strip, White, 60 pixels per meter.
