# Fritzing sketch FeatherHuzzahESP8266Hookup (saved by Fritzing 0.9.3b)

parts:
  NEOPIXEL1 = Neopixel Strip -- White (60/m) [part_number=1138]
  NEOPIXEL2 = Neopixel Strip -- White (60/m) [part_number=1138]
  Part1 = Adafruit Feather HUZZAH ESP8266 [part_number="Adafruit #2821"]

nets:
  +5V: NEOPIXEL1.+5V, NEOPIXEL2.+5V, Part1.3.3V
  N1: NEOPIXEL1.DI, Part1.GPIO4/SDA
  GND: NEOPIXEL1.GND, NEOPIXEL2.GND, Part1.GND
  N2: NEOPIXEL2.DI, Part1.GPIO5/SCL

custom parts:
  Neopixel Strip -- White (60/m): Neopixel Strip, White, 60 pixels per meter.
  Adafruit Feather HUZZAH ESP8266: his is the Adafruit Feather HUZZAH ESP8266 - our take on an 'all-in-one' ESP8266 WiFi development board with built in USB and battery charging. Its an ESP8266 WiFi module with all the extras you need, ready to rock! We have other boards in the Feather family, check'em out here. At the Feather HUZZAH's heart is an ESP8266 WiFi microcontroller clocked at 80 MHz and at 3.3V logic. This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
